# Fritzing sketch iron_man_guanlet_schematics (saved by Fritzing 0.7.9b)
breadboards: 1

parts:
  R1 = Resistor [tolerance=±5% resistance=220 package=THT]
  R2 = Resistor [tolerance=±5% resistance=220 package=THT]
  LED1 = LED - 5mm [color="White (4500K)" package="5 mm [THT]"]
  LED2 = LED - 5mm [color="Blue (470nm)" package="5 mm [THT]"]
  Arduino1 = Arduino
  3-Axis_Accelerometer1 = 3-Axis Accelerometer Breakout - MMA8452Q
  SPKR1 = Loudspeaker

nets:
  N1: R1.Pin_0, LED2.cathode, Arduino1.D6
  GND: R1.Pin_1, R2.Pin_1, LED1.anode, LED2.anode, Arduino1.GND, 3-Axis_Accelerometer1.GND, SPKR1.pin1
  N2: R2.Pin_0, LED1.cathode, Arduino1.D5
  N3: Arduino1.D11, SPKR1.pin2
  3V3: Arduino1.3V3, 3-Axis_Accelerometer1.3.3V
  N4: Arduino1.A2, 3-Axis_Accelerometer1.I1
  N5: Arduino1.A3, 3-Axis_Accelerometer1.I2
  N6: Arduino1.A4, 3-Axis_Accelerometer1.SDA
  N7: Arduino1.A5, 3-Axis_Accelerometer1.SCL
